# Fritzing sketch transit-notifier - resistors (saved by Fritzing 0.9.3b)
circuit board: 9.77cm x 7.19805cm
breadboards: 3

parts:
  CAP1188_0x29 = Adafruit CAP1188 - 8-Key Capacitive Touch Sensor Breakout [part_number="Adafruit #1602"]
  Map_lights = male pin header, 4 pins [form="♂ (male)"]
  Program_(RX/TX) = male pin header, 2 pins [form="♂ (male)"]
  Power = Power plug
  CAP1188_0x28 = Adafruit CAP1188 - 8-Key Capacitive Touch Sensor Breakout [part_number="Adafruit #1602"]
  Adafruit_HUZZAH = Adafruit HUZZAH ESP8266 Breakout [part_number=2471]
  Indicators = double row male pin header, 10 pins [form="♂ (male)"]
  1-16_bus_stops = double row male pin header, 16 pins [form="♂ (male)"]
  R10 = Resistor [tolerance=±5% resistance=1k package=THT]
  R9 = Resistor [tolerance=±5% resistance=1k package=THT]
  R12 = Resistor [tolerance=±5% resistance=1k package=THT]
  R1 = Resistor [tolerance=±5% resistance=1k package=THT]
  R2 = Resistor [tolerance=±5% resistance=1k package=THT]
  R3 = Resistor [tolerance=±5% resistance=1k package=THT]
  R4 = Resistor [tolerance=±5% resistance=1k package=THT]
  R5 = Resistor [tolerance=±5% resistance=1k package=THT]
  R6 = Resistor [tolerance=±5% resistance=1k package=THT]
  R7 = Resistor [tolerance=±5% resistance=1k package=THT]
  R8 = Resistor [tolerance=±5% resistance=1k package=THT]
  R11 = Resistor [tolerance=±5% resistance=1k package=THT]
  R13 = Resistor [tolerance=±5% resistance=1k package=THT]
  R14 = Resistor [tolerance=±5% resistance=1k package=THT]
  R15 = Resistor [tolerance=±5% resistance=1k package=THT]
  R16 = Resistor [tolerance=±5% resistance=1k package=THT]

nets:
  N1: CAP1188_0x29.CS1, R8.Pin_0
  N2: CAP1188_0x29.CS2, R7.Pin_0
  N3: CAP1188_0x29.CS3, R6.Pin_0
  N4: CAP1188_0x29.CS4, R5.Pin_0
  N5: CAP1188_0x29.CS5, R4.Pin_0
  N6: CAP1188_0x29.CS6, R3.Pin_0
  N7: CAP1188_0x29.CS7, R2.Pin_0
  N8: CAP1188_0x29.CS8, R1.Pin_0
  N9: CAP1188_0x29.SDA/MISO, CAP1188_0x28.SDA/MISO, Adafruit_HUZZAH.#4
  N10: CAP1188_0x29.SCK, CAP1188_0x28.SCK, Adafruit_HUZZAH.#5
  VIN: CAP1188_0x29.VIN, Map_lights.pin1, Power.VCC, CAP1188_0x28.VIN, Adafruit_HUZZAH.VBat, Indicators.pin5, Indicators.pin6
  GND: CAP1188_0x29.GND, Map_lights.pin4, Power.GND, CAP1188_0x28.GND, Adafruit_HUZZAH.GND, Indicators.pin2, Indicators.pin9, Indicators.pin10
  N11: Map_lights.pin2, Adafruit_HUZZAH.#13
  N12: Map_lights.pin3, Adafruit_HUZZAH.#12
  N13: Program_(RX/TX).pin1, Adafruit_HUZZAH.TX
  N14: Program_(RX/TX).pin2, Adafruit_HUZZAH.RX
  N15: CAP1188_0x28.3.3V, CAP1188_0x28.ADDR
  N16: CAP1188_0x28.CS1, R16.Pin_0
  N17: CAP1188_0x28.CS2, R15.Pin_0
  N18: CAP1188_0x28.CS3, R14.Pin_0
  N19: CAP1188_0x28.CS4, R13.Pin_0
  N20: CAP1188_0x28.CS5, R12.Pin_0
  N21: CAP1188_0x28.CS6, R11.Pin_0
  N22: CAP1188_0x28.CS7, R10.Pin_0
  N23: CAP1188_0x28.CS8, R9.Pin_0
  N24: Adafruit_HUZZAH.#14, Indicators.pin7
  N25: Adafruit_HUZZAH.#16, Indicators.pin8
  N26: Adafruit_HUZZAH.RST, Indicators.pin1
  N27: Adafruit_HUZZAH.#2, Indicators.pin4
  N28: Adafruit_HUZZAH.#15, Indicators.pin3
  N29: 1-16_bus_stops.pin1, R16.Pin_1
  N30: 1-16_bus_stops.pin2, R15.Pin_1
  N31: 1-16_bus_stops.pin3, R14.Pin_1
  N32: 1-16_bus_stops.pin4, R13.Pin_1
  N33: 1-16_bus_stops.pin5, R12.Pin_1
  N34: 1-16_bus_stops.pin6, R11.Pin_1
  N35: 1-16_bus_stops.pin7, R10.Pin_1
  N36: 1-16_bus_stops.pin8, R9.Pin_1
  N37: 1-16_bus_stops.pin9, R8.Pin_1
  N38: 1-16_bus_stops.pin10, R7.Pin_1
  N39: 1-16_bus_stops.pin11, R6.Pin_1
  N40: 1-16_bus_stops.pin12, R5.Pin_1
  N41: 1-16_bus_stops.pin13, R4.Pin_1
  N42: 1-16_bus_stops.pin14, R3.Pin_1
  N43: 1-16_bus_stops.pin15, R2.Pin_1
  N44: 1-16_bus_stops.pin16, R1.Pin_1

notes:
  Transit Notifier, 5ynco - Bus Aid - Diego and Shambhavi, 1

custom parts:
  Adafruit CAP1188 - 8-Key Capacitive Touch Sensor Breakout: Add lots of touch sensors to your next microcontroller project with this easy-to-use 8-channel capacitive touch sensor breakout board, starring the CAP1188. This chip can handle up to 8 individual touch pads, and has a very nice feature that makes it stand out for us: it will light up the 8 onboard LEDs when the matching touch sensor fires to help you debug your sensor setup. The CAP1188 has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
