# Fritzing sketch transit-notifier (saved by Fritzing 0.9.3b)
circuit board: 9.79376cm x 6.60416cm
breadboards: 3

parts:
  CAP1188_0x29 = Adafruit CAP1188 - 8-Key Capacitive Touch Sensor Breakout [part_number="Adafruit #1602"]
  Stop_lights = male pin header, 4 pins [form="♂ (male)"]
  Program_(RX/TX) = male pin header, 2 pins [form="♂ (male)"]
  Power = Power plug
  CAP1188_0x28 = Adafruit CAP1188 - 8-Key Capacitive Touch Sensor Breakout [part_number="Adafruit #1602"]
  1-16_bus_stops = double row male pin header, 16 pins [form="♂ (male)"]
  Routes_lights = double row male pin header, 10 pins [form="♂ (male)"]
  Adafruit_HUZZAH = Adafruit HUZZAH ESP8266 Breakout [part_number=2471]

nets:
  N1: CAP1188_0x29.CS1, 1-16_bus_stops.pin9
  N2: CAP1188_0x29.CS2, 1-16_bus_stops.pin10
  N3: CAP1188_0x29.CS3, 1-16_bus_stops.pin11
  N4: CAP1188_0x29.CS4, 1-16_bus_stops.pin12
  N5: CAP1188_0x29.CS5, 1-16_bus_stops.pin13
  N6: CAP1188_0x29.CS6, 1-16_bus_stops.pin14
  N7: CAP1188_0x29.CS7, 1-16_bus_stops.pin15
  N8: CAP1188_0x29.CS8, 1-16_bus_stops.pin16
  N9: CAP1188_0x29.SDA/MISO, CAP1188_0x28.SDA/MISO, Adafruit_HUZZAH.#4
  N10: CAP1188_0x29.SCK, CAP1188_0x28.SCK, Adafruit_HUZZAH.#5
  VIN: CAP1188_0x29.VIN, Stop_lights.pin1, Power.VCC, CAP1188_0x28.VIN, Routes_lights.pin5, Routes_lights.pin6, Adafruit_HUZZAH.VBat
  GND: CAP1188_0x29.GND, Stop_lights.pin4, Power.GND, CAP1188_0x28.GND, Routes_lights.pin2, Routes_lights.pin9, Routes_lights.pin10, Adafruit_HUZZAH.GND
  N11: Stop_lights.pin2, Adafruit_HUZZAH.#13
  N12: Stop_lights.pin3, Adafruit_HUZZAH.#12
  N13: Program_(RX/TX).pin1, Adafruit_HUZZAH.TX
  N14: Program_(RX/TX).pin2, Adafruit_HUZZAH.RX
  N15: CAP1188_0x28.3.3V, CAP1188_0x28.ADDR
  N16: CAP1188_0x28.CS1, 1-16_bus_stops.pin1
  N17: CAP1188_0x28.CS2, 1-16_bus_stops.pin2
  N18: CAP1188_0x28.CS3, 1-16_bus_stops.pin3
  N19: CAP1188_0x28.CS4, 1-16_bus_stops.pin4
  N20: CAP1188_0x28.CS5, 1-16_bus_stops.pin5
  N21: CAP1188_0x28.CS6, 1-16_bus_stops.pin6
  N22: CAP1188_0x28.CS7, 1-16_bus_stops.pin7
  N23: CAP1188_0x28.CS8, 1-16_bus_stops.pin8
  N24: Routes_lights.pin1, Adafruit_HUZZAH.RST
  N25: Routes_lights.pin3, Adafruit_HUZZAH.#15
  N26: Routes_lights.pin4, Adafruit_HUZZAH.#2
  N27: Routes_lights.pin7, Adafruit_HUZZAH.#14
  N28: Routes_lights.pin8, Adafruit_HUZZAH.#16

notes:
  Transit Notifier, 5ynco - Bus Aid - Diego and Shambhavi, 1

custom parts:
  Adafruit CAP1188 - 8-Key Capacitive Touch Sensor Breakout: Add lots of touch sensors to your next microcontroller project with this easy-to-use 8-channel capacitive touch sensor breakout board, starring the CAP1188. This chip can handle up to 8 individual touch pads, and has a very nice feature that makes it stand out for us: it will light up the 8 onboard LEDs when the matching touch sensor fires to help you debug your sensor setup. The CAP1188 has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
